# Fritzing sketch elec (saved by Fritzing 0.9.9b)
breadboards: 1

parts:
  LED1 = LEDs [package=led10mm]
  Q1 = NPN-Transistor [package="SOT-23 [SMD]"]
  R1 = Resistor [tolerance=±5% power=0.25 resistance=220 package=THT]
  MCU1 = Raspberry Pi Zero
  IR1 = TSOP312.., 314.. [package=THT]

nets:
  N1: LED1.C, Q1.1
  N2: LED1.A, MCU1.pin_2, MCU1.pin_4, IR1.Data
  N3: Q1.2, MCU1.pin_6, MCU1.pin_39, IR1.GND
  N4: Q1.0, R1.Pin_0
  N5: R1.Pin_1, MCU1.pin_37
  N6: MCU1.pin_35, IR1.Vs
